// Logisim project schema.circ as structural Verilog: 2 circuits, main circuit main
module main (
);

  wire and_1_out, and_2_out, clk_i, comparator_1_eq, comparator_2_eq, comparator_3_eq, comparator_4_eq,
       d_ff_1_q, en_ctrl_cpt_s, en_reg1, en_reg1_s, en_reg2_s, en_reg3_s, en_reg4_s, not_1_out, or_1_out,
       read_i, readdatavalid_o, reset_i, waitrequest_o, write_i;
  wire [1:0] mss_1_state_s;
  wire [2:0] address_i;
  wire [3:0] byteenable_i;
  wire [31:0] adder_1_out, cpt_pres_s, CSTE, data_masked_s, multiplexer_6_out, multiplexer_7_out, readdata_o,
       reg1_pres_s, reg2_pres_s, reg3_pres_s, reg4_pres_s, writedata_i;

  Multiplexer #(.width(8), .enable("false")) multiplexer_1 (
    .in0(readdata_o[23:16]), .in1(writedata_i[23:16]), .out(data_masked_s[23:16]), .sel(byteenable_i[2]));
  Multiplexer #(.width(8), .enable("false")) multiplexer_2 (
    .in0(readdata_o[31:24]), .in1(writedata_i[31:24]), .out(data_masked_s[31:24]), .sel(byteenable_i[3]));
  Demultiplexer #(.select(3), .enable("false")) demultiplexer_1 (
    .out2(en_ctrl_cpt_s), .out3(en_reg1_s), .out4(en_reg2_s), .out5(en_reg3_s), .out6(en_reg4_s),
    .in(write_i), .sel(address_i));  // open: out0, out1, out7
  Multiplexer #(.select(3), .width(32), .enable("false")) multiplexer_3 (
    .in0(CSTE), .in1(cpt_pres_s), .in2({32{1'b0}}), .in3(reg1_pres_s), .in4(reg2_pres_s), .in5(reg3_pres_s),
    .in6(reg4_pres_s), .in7({32{1'b0}}), .out(readdata_o), .sel(address_i));
  Multiplexer #(.width(8), .enable("false")) multiplexer_4 (
    .in0(readdata_o[7:0]), .in1(writedata_i[7:0]), .out(data_masked_s[7:0]), .sel(byteenable_i[0]));
  Multiplexer #(.width(8), .enable("false")) multiplexer_5 (
    .in0(readdata_o[15:8]), .in1(writedata_i[15:8]), .out(data_masked_s[15:8]), .sel(byteenable_i[1]));
  D_Flip_Flop d_ff_1 (.D(en_ctrl_cpt_s), .clk(clk_i), .Q(d_ff_1_q), .reset(reset_i));  // open: Qn, preset
  Adder #(.width(32)) adder_1 (.a(cpt_pres_s), .b(32'h1), .out(adder_1_out));  // open: cin, cout
  Comparator #(.width(32)) comparator_1 (.a(data_masked_s), .b(32'h2), .eq(comparator_1_eq));  // open: gt, lt
  not not_1 (not_1_out, d_ff_1_q);
  Multiplexer #(.width(32), .enable("false")) multiplexer_6 (
    .in0(cpt_pres_s), .in1(adder_1_out), .out(multiplexer_6_out), .sel(and_1_out));
  and and_1 (and_1_out, comparator_1_eq, and_2_out);
  and and_2 (and_2_out, en_ctrl_cpt_s, not_1_out);
  MSS mss_1 (.read_i(read_i), .write_i(write_i), .clk_i(clk_i), .reset_i(reset_i), .state_s(mss_1_state_s));
  Register #(.width(32)) reg1 (.D(data_masked_s), .en(en_reg1), .clk(reset_i), .Q(reg1_pres_s), .clr(clk_i));
  Multiplexer #(.width(32), .enable("false")) multiplexer_7 (
    .in0(multiplexer_6_out), .in1({32{1'b0}}), .out(multiplexer_7_out), .sel(comparator_2_eq));
  Comparator #(.width(32)) comparator_2 (.a(data_masked_s), .b(32'h1), .eq(comparator_2_eq));  // open: gt, lt
  Comparator #(.width(2)) comparator_3 (.a(mss_1_state_s), .b(2'b01), .eq(comparator_3_eq));  // open: gt, lt
  Comparator #(.width(2)) comparator_4 (.a(mss_1_state_s), .b(2'b00), .eq(comparator_4_eq));  // open: gt, lt
  or or_1 (or_1_out, read_i, write_i);
  and and_3 (readdatavalid_o, read_i, comparator_3_eq);
  and and_4 (waitrequest_o, comparator_4_eq, or_1_out);
  Register #(.width(32)) cpt (.D(multiplexer_7_out), .en(en_ctrl_cpt_s), .clk(reset_i), .Q(cpt_pres_s), .clr(clk_i));

  // Notes on the sheet:
  //   Attention, votre version de Logisim
  //   ne contient pas de tracker. Si vous
  //   enregistrez votre projet, toutes les
  //   informations du tracker seront
  //   définitivement effacées.
  //   byte 3
  //   byte 0
  //   détection de flanc pour incrémenter 1 seule fois
  //   idem pour reg2,3,4
endmodule

module MSS (
  input  read_i,
  input  write_i,
  input  clk_i,
  input  reset_i,
  output [1:0] state_s
);

  wire and_1_out, and_2_out, and_3_out, and_4_out, not_1_out, not_2_out, or_1_out;
  wire [2:0] state0_q;

  not not_1 (not_1_out, read_i);
  not not_2 (not_2_out, write_i);
  and and_1 (and_1_out, not_1_out, state0_q[1]);
  and and_2 (and_2_out, not_2_out, state0_q[2]);
  or or_1 (or_1_out, and_1_out, and_2_out, reset_i);
  and and_3 (and_3_out, state0_q[0], read_i);
  and and_4 (and_4_out, state0_q[0], write_i);
  D_Flip_Flop state0 (.D(or_1_out), .clk(clk_i), .Q(state0_q[0]), .reset(reset_i));  // open: Qn, preset
  D_Flip_Flop state1 (.D(and_3_out), .clk(clk_i), .Q(state0_q[1]), .reset(reset_i));  // open: Qn, preset
  D_Flip_Flop state2 (.D(and_4_out), .clk(clk_i), .Q(state0_q[2]), .reset(reset_i));  // open: Qn, preset
  Multiplexer #(.select(3), .width(2), .enable("false")) multiplexer_1 (
    .in0(2'b00), .in1(2'b00), .in2(2'b01), .in3(2'b00), .in4(2'b10), .in5(2'b00), .in6(2'b00), .in7(2'b00),
    .out(state_s), .sel(state0_q));

  // Other names for the same wires on the sheet: clk = clk_i; rst = reset_i

  // Notes on the sheet:
  //   Attention, votre version de Logisim
  //   ne contient pas de tracker. Si vous
  //   enregistrez votre projet, toutes les
  //   informations du tracker seront
  //   définitivement effacées.
endmodule
